# Fritzing sketch rc-tx-rx (saved by Fritzing 0.9.6b)

parts:
  MH-ET_Live_Minikit_for_ESP1 = MH-ET Live Minikit for ESP32
  M1 = MT3608 Module
  M2 = TP4056 Module [part_number=HW-107]
  U1 = LIPO-1000mAh [package=lipo-1000]
  Part1 = Thumb Joystick
  S1 = Toggle Switch [package=THT]
  MH-ET_Live_Minikit_for_ESP2 = MH-ET Live Minikit for ESP32
  M3 = MT3608 Module
  M4 = TP4056 Module [part_number=HW-107]
  U2 = LIPO-1000mAh [package=lipo-1000]
  S2 = Toggle Switch [package=THT]
  S3 = H-Bridge with L298N
  M5 = gear-motor
  M6 = gear-motor
  Part2 = 12 NeoPixel Ring [part_number=1643]
  LED1 = smd LED [color="Red (633nm)" package="0805 [SMD]"]
  LED2 = smd LED [color="Red (633nm)" package="0805 [SMD]"]
  R1 = Resistor [tolerance=±5% resistance=330 package="0603 [SMD]"]
  R2 = Resistor [tolerance=±5% resistance=330 package="0603 [SMD]"]

nets:
  GND: MH-ET_Live_Minikit_for_ESP1.GND, M1.pin4, Part1.GND
  N1: MH-ET_Live_Minikit_for_ESP1.IO33, Part1.HORZ
  N2: MH-ET_Live_Minikit_for_ESP1.IO34, Part1.VERT
  N3: MH-ET_Live_Minikit_for_ESP1.IO18, Part1.SEL
  3.3V: MH-ET_Live_Minikit_for_ESP1.3.3V, Part1.VCC
  N4: MH-ET_Live_Minikit_for_ESP1.VCC, M1.pin3
  N5: M1.pin1, M2.OUT-#1
  N6: M1.pin2, S1.L1
  N7: M2.BAT-, U1.-
  N8: M2.BAT+, U1.+
  N9: M2.OUT-#4, S1.COM
  GND_2: MH-ET_Live_Minikit_for_ESP2.GND, M3.pin4, S3.GND, Part2.GND, LED1.anode, LED2.anode
  N10: MH-ET_Live_Minikit_for_ESP2.IO17, S3.IN2
  N11: MH-ET_Live_Minikit_for_ESP2.IO16, S3.IN4
  VCC: MH-ET_Live_Minikit_for_ESP2.VCC, M3.pin3, Part2.VDD
  N12: MH-ET_Live_Minikit_for_ESP2.IO32, S3.IN1
  N13: MH-ET_Live_Minikit_for_ESP2.TDI, S3.IN3
  N14: MH-ET_Live_Minikit_for_ESP2.IO4, Part2.IN
  N15: MH-ET_Live_Minikit_for_ESP2.IO0, R2.Pin_0
  N16: M3.pin1, M4.OUT-#1
  N17: M3.pin2, S2.L1
  N18: M4.BAT-, U2.-
  N19: M4.BAT+, U2.+
  N20: M4.OUT-#4, S2.COM
  N21: S3.M1-01, M6.pin_2
  N22: S3.M1-02, M6.pin_1
  N23: S3.M2-01, M5.pin_2
  N24: S3.M2-02, M5.pin_1
  N25: LED1.cathode, R1.Pin_1
  N26: LED2.cathode, R2.Pin_1

notes:
  ESP32 Battery Powered Radio Controller - Transmitter
  Reset and Flash by RTS and DTR
  ESP32 Battery Powered Radio Controller - Receiver

custom parts:
  MH-ET Live Minikit for ESP32: MH-ET Live Minikit for ESP32 ( http://mh.nodebb.com/topic/8/mh-et-live-minikit-for-esp32/2/) PCB footprint is invalid.
  MT3608 Module: MT3608 Boost Converter Module Links: Aerosemi MT3608 2A Step Up Converter datasheet
  TP4056 Module: TP4056 Lithium Battery Charge Management Module Links: TP4056 website
  H-Bridge with L298N: h-bridge
  12 NeoPixel Ring: 12 ultra bright smart LED NeoPixels are arranged in a circle with 1.5" (37mm) outer diameter. The rings are 'chainable' - connect the output pin of one to the input pin of another. Use only one microcontroller pin to control as many as you can chain together! Each LED is addressable as the driver chip is inside the LED. Each one has ~18mA constant current drive so the color will be very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
